# Fritzing sketch sketch (saved by Fritzing 0.9.3b)
breadboards: 1

parts:
  Part1 = Arduino Nano (Rev3.0)
  HC-SR04_Sensor_1 = HC-SR04 Ultrasonic Distance Sensor
  NEOPIXEL1 = Neopixel Strip -- White (60/m)

nets:
  N1: Part1.D2, HC-SR04_Sensor_1.ECHO
  N2: Part1.D3, HC-SR04_Sensor_1.TRIG
  N3: Part1.D5, NEOPIXEL1.+5V
  GND: Part1.GND, HC-SR04_Sensor_1.GND, NEOPIXEL1.GND
  5V: Part1.5V, HC-SR04_Sensor_1.VCC, NEOPIXEL1.DI

custom parts:
  Neopixel Strip -- White (60/m): Neopixel Strip, White, 60 pixels per meter.
